# Fritzing sketch 2.1.1_Button (saved by Fritzing 0.9.3b)
breadboards: 1

parts:
  T-Cobbler1 = T-Cobbler
  LED1 = LED - 5mm [color="Red (633nm)" package="5 mm [THT]"]
  R1 = Resistor [tolerance=±5% resistance=220 package=THT]
  S1 = Pushbutton [package="[THT]"]

nets:
  N1: T-Cobbler1.3V3, R1.Pin_1
  N2: T-Cobbler1.GND#4, S1.Pin_1, S1.Pin_2
  N3: T-Cobbler1.#17, LED1.cathode
  N4: T-Cobbler1.#18, S1.Pin_3, S1.Pin_4
  N5: LED1.anode, R1.Pin_0

custom parts:
  T-Cobbler: T-Cobbler for RPi B+ and Rpi2 from SunFounder
  Pushbutton: A generic pushbutton.
