# Fritzing sketch 2.1.4_Potentiometer (saved by Fritzing 0.9.3b)
breadboards: 1

parts:
  T-Cobbler1 = T-Cobbler
  IC1 = IC, DIP package, 16 pins [chip_label=PCF8591]
  R1 = Potentiometer [package=THT]
  R2 = Resistor [tolerance=±5% resistance=10k package=THT]
  R3 = Resistor [tolerance=±5% resistance=10k package=THT]
  R4 = Resistor [tolerance=±5% resistance=220 package=THT]
  LED1 = LED - 5mm [color="Red (633nm)" package="5 mm [THT]"]

nets:
  N1: T-Cobbler1.SDA, IC1.pin9, R3.Pin_0
  N2: T-Cobbler1.SCL, IC1.pin10, R2.Pin_0
  N3: T-Cobbler1.3.3V, IC1.pin14, IC1.pin16, R1.leg1, R2.Pin_1, R3.Pin_1
  N4: T-Cobbler1.GND#22, IC1.pin5, IC1.pin6, IC1.pin7, IC1.pin8, IC1.pin12, IC1.pin13, R1.leg2, LED1.cathode
  N5: IC1.pin1, R1.wiper
  N6: IC1.pin15, R4.Pin_1
  N7: R4.Pin_0, LED1.anode

custom parts:
  T-Cobbler: T-Cobbler for RPi B+ and Rpi2 from SunFounder
  Potentiometer: A standard adjustable resistor (potentiometer).
