# Fritzing sketch 2.1.5_Keypad (saved by Fritzing 0.9.3b)
breadboards: 1

parts:
  T-Cobbler1 = T-Cobbler
  IC2 = 4*4 keyboard [chip_label=IC package="DIP (Dual Inline) [THT]"]

nets:
  N1: T-Cobbler1.#17, IC2.Y4
  N2: T-Cobbler1.#27, IC2.Y3
  N3: T-Cobbler1.#22, IC2.Y2
  N4: T-Cobbler1.MOSI, IC2.Y1
  N5: T-Cobbler1.#18, IC2.X1
  N6: T-Cobbler1.#23, IC2.X2
  N7: T-Cobbler1.#24, IC2.X3
  N8: T-Cobbler1.#25, IC2.X4

custom parts:
  T-Cobbler: T-Cobbler for RPi B+ and Rpi2 from SunFounder
  4*4 keyboard: A 4*4 keyboard
