# Fritzing sketch 2.1.6_Joystick (saved by Fritzing 0.9.3b)
breadboards: 1

parts:
  T-Cobbler1 = T-Cobbler
  IC1 = IC, DIP package, 16 pins [chip_label=PCF8591]
  R2 = Resistor [tolerance=±5% resistance=10k package=THT]
  R3 = Resistor [tolerance=±5% resistance=10k package=THT]
  S2 = Joystick PS2 v1.0 [package=THT]

nets:
  N1: T-Cobbler1.SDA, IC1.pin9, R3.Pin_0
  N2: T-Cobbler1.SCL, IC1.pin10, R2.Pin_0
  N3: T-Cobbler1.#17, S2.SW
  3.3V: T-Cobbler1.3.3V, IC1.pin14, IC1.pin16, R2.Pin_1, R3.Pin_1, S2.VCC
  N4: T-Cobbler1.GND#22, IC1.pin5, IC1.pin6, IC1.pin7, IC1.pin8, IC1.pin12, IC1.pin13, S2.GND
  N5: IC1.pin1, S2.VRY
  N6: IC1.pin2, S2.VRX

custom parts:
  T-Cobbler: T-Cobbler for RPi B+ and Rpi2 from SunFounder
  Joystick PS2 v1.0: A joystick is an input device consisting of a stick that pivots on a base and reports its angle or direction to the device it is controlling. Joysticks are often used to control video games and robots. A Joystick PS2 is used here.
