# Fritzing sketch 2.2.2_Thermistor (saved by Fritzing 0.9.3b)
breadboards: 1

parts:
  T-Cobbler1 = T-Cobbler
  IC1 = IC, DIP package, 16 pins [chip_label=PCF8591]
  R2 = Resistor [tolerance=±5% resistance=10k package=THT]
  R3 = Resistor [tolerance=±5% resistance=10k package=THT]
  R5 = Resistor [tolerance=±5% resistance=10k package=THT]
  R6 = Temperature Sensor (Thermistor) [thermistor_type=NTC package=THT]

nets:
  N1: T-Cobbler1.SDA, IC1.pin9, R3.Pin_0
  N2: T-Cobbler1.SCL, IC1.pin10, R2.Pin_0
  N3: T-Cobbler1.3.3V, IC1.pin14, IC1.pin16, R2.Pin_1, R3.Pin_1, R5.Pin_1
  N4: T-Cobbler1.GND#22, IC1.pin5, IC1.pin6, IC1.pin7, IC1.pin8, IC1.pin12, IC1.pin13, R6.pin_1
  N5: IC1.pin1, R5.Pin_0, R6.pin_0

custom parts:
  T-Cobbler: T-Cobbler for RPi B+ and Rpi2 from SunFounder
