# Fritzing sketch 3.1.3_PasswordLock (saved by Fritzing 0.9.3b)
breadboards: 1

parts:
  T-Cobbler1 = T-Cobbler
  IC2 = 4*4 keyboard [chip_label=IC package="DIP (Dual Inline) [THT]"]
  module1 = I2C LCD1602

nets:
  N1: T-Cobbler1.SDA, module1.SDA
  N2: T-Cobbler1.SCL, module1.SCL
  N3: T-Cobbler1.#17, IC2.Y4
  N4: T-Cobbler1.#27, IC2.Y3
  N5: T-Cobbler1.#22, IC2.Y2
  N6: T-Cobbler1.MOSI, IC2.Y1
  N7: T-Cobbler1.5.0V#20, module1.VCC
  N8: T-Cobbler1.GND#22, module1.GND
  N9: T-Cobbler1.#18, IC2.X1
  N10: T-Cobbler1.#23, IC2.X2
  N11: T-Cobbler1.#24, IC2.X3
  N12: T-Cobbler1.#25, IC2.X4

custom parts:
  T-Cobbler: T-Cobbler for RPi B+ and Rpi2 from SunFounder
  4*4 keyboard: A 4*4 keyboard
  I2C LCD1602: I2C LCD1602 module of SunFounder Sensor Kit
